// Logisim project Assignment4_a.circ as structural Verilog: 5 circuits, main circuit RAM8
module RAM8 (
  input  load,
  input  [2:0] address,
  input  [15:0] in,
  output [15:0] out
);

  wire clock_1_out, demultiplexer_1_out0, demultiplexer_1_out1, demultiplexer_1_out2, demultiplexer_1_out3,
       demultiplexer_1_out4, demultiplexer_1_out5, demultiplexer_1_out6, demultiplexer_1_out7;
  wire [15:0] register_1_q, register_2_q, register_3_q, register_4_q, register_5_q, register_6_q,
       register_7_q, register_8_q;

  Demultiplexer #(.enable("false"), .select(3)) demultiplexer_1 (
    .out0(demultiplexer_1_out0), .out1(demultiplexer_1_out1), .out2(demultiplexer_1_out2),
    .out3(demultiplexer_1_out3), .out4(demultiplexer_1_out4), .out5(demultiplexer_1_out5),
    .out6(demultiplexer_1_out6), .out7(demultiplexer_1_out7), .in(load), .sel(address));
  Clock clock_1 (.out(clock_1_out));
  Register #(.width(16)) register_1 (
    .D(in), .en(demultiplexer_1_out0), .clk(clock_1_out), .Q(register_1_q));  // open: clr
  Register #(.width(16)) register_2 (
    .D(in), .en(demultiplexer_1_out1), .clk(clock_1_out), .Q(register_2_q));  // open: clr
  Register #(.width(16)) register_3 (
    .D(in), .en(demultiplexer_1_out2), .clk(clock_1_out), .Q(register_3_q));  // open: clr
  Register #(.width(16)) register_4 (
    .D(in), .en(demultiplexer_1_out3), .clk(clock_1_out), .Q(register_4_q));  // open: clr
  Register #(.width(16)) register_5 (
    .D(in), .en(demultiplexer_1_out4), .clk(clock_1_out), .Q(register_5_q));  // open: clr
  Register #(.width(16)) register_6 (
    .D(in), .en(demultiplexer_1_out5), .clk(clock_1_out), .Q(register_6_q));  // open: clr
  Register #(.width(16)) register_7 (
    .D(in), .en(demultiplexer_1_out6), .clk(clock_1_out), .Q(register_7_q));  // open: clr
  Register #(.width(16)) register_8 (
    .D(in), .en(demultiplexer_1_out7), .clk(clock_1_out), .Q(register_8_q));  // open: clr
  Register #(.width(16)) register_9 ();  // open: D, en, clk, Q, clr
  Multiplexer #(.enable("false"), .select(3), .width(16)) multiplexer_1 (
    .in0(register_1_q), .in1(register_2_q), .in2(register_3_q), .in3(register_4_q), .in4(register_5_q),
    .in5(register_6_q), .in6(register_7_q), .in7(register_8_q), .out(out), .sel(address));

  // Notes on the sheet:
  //   Function:
  //   out(t) = RAM[address(t)](t)
  //   If load(t-1) then 
  //   	RAM[address(t - 1)](t) = in(t-1)
  //   To implement a RAM8 chip, you can line up an array of 8 registers. The next step is to build combinational
  //   logic that, given a certain address value, takes the RAM8's in input and only loads it into the selected register.
  //   In a similar fashion, you have to build combinational logic that, given a certain address value, selects the right
  //   register and pipes its out value to the RAM8's out output.
  //   Tip: The combinational logic was already built in Assignment 1
  //   You are allowed to use and copy the below component
endmodule

module Register_File (
  input  load,
  input  [2:0] Write_Address,
  input  [15:0] Write_Data,
  input  [2:0] Read_Address_1,
  input  [2:0] Read_Address_2,
  output [15:0] Read_Data_1,
  output [15:0] Read_Data_2
);

  wire clock_1_out, demultiplexer_1_out0, demultiplexer_1_out1, demultiplexer_1_out2, demultiplexer_1_out3,
       demultiplexer_1_out4, demultiplexer_1_out5, demultiplexer_1_out6, demultiplexer_1_out7;
  wire [15:0] register_1_q, register_2_q, register_3_q, register_4_q, register_5_q, register_6_q,
       register_7_q, register_8_q;

  Demultiplexer #(.enable("false"), .select(3)) demultiplexer_1 (
    .out0(demultiplexer_1_out0), .out1(demultiplexer_1_out1), .out2(demultiplexer_1_out2),
    .out3(demultiplexer_1_out3), .out4(demultiplexer_1_out4), .out5(demultiplexer_1_out5),
    .out6(demultiplexer_1_out6), .out7(demultiplexer_1_out7), .in(load), .sel(Write_Address));
  Clock clock_1 (.out(clock_1_out));
  Register #(.width(16)) register_1 (
    .D(Write_Data), .en(demultiplexer_1_out0), .clk(clock_1_out), .Q(register_1_q));  // open: clr
  Register #(.width(16)) register_2 (
    .D(Write_Data), .en(demultiplexer_1_out1), .clk(clock_1_out), .Q(register_2_q));  // open: clr
  Register #(.width(16)) register_3 (
    .D(Write_Data), .en(demultiplexer_1_out2), .clk(clock_1_out), .Q(register_3_q));  // open: clr
  Register #(.width(16)) register_4 (
    .D(Write_Data), .en(demultiplexer_1_out3), .clk(clock_1_out), .Q(register_4_q));  // open: clr
  Register #(.width(16)) register_5 (
    .D(Write_Data), .en(demultiplexer_1_out4), .clk(clock_1_out), .Q(register_5_q));  // open: clr
  Register #(.width(16)) register_6 (
    .D(Write_Data), .en(demultiplexer_1_out5), .clk(clock_1_out), .Q(register_6_q));  // open: clr
  Register #(.width(16)) register_7 (
    .D(Write_Data), .en(demultiplexer_1_out6), .clk(clock_1_out), .Q(register_7_q));  // open: clr
  Register #(.width(16)) register_8 (
    .D(Write_Data), .en(demultiplexer_1_out7), .clk(clock_1_out), .Q(register_8_q));  // open: clr
  Multiplexer #(.enable("false"), .select(3), .width(16)) multiplexer_1 (
    .in0(register_1_q), .in1(register_2_q), .in2(register_3_q), .in3(register_4_q), .in4(register_5_q),
    .in5(register_6_q), .in6(register_7_q), .in7(register_8_q), .out(Read_Data_1), .sel(Read_Address_1));
  Multiplexer #(.enable("false"), .select(3), .width(16)) multiplexer_2 (
    .in0(register_1_q), .in1(register_2_q), .in2(register_3_q), .in3(register_4_q), .in4(register_5_q),
    .in5(register_6_q), .in6(register_7_q), .in7(register_8_q), .out(Read_Data_2), .sel(Read_Address_2));

  // Notes on the sheet:
  //   Function:
  //   Read Data 1 = Register File[Read Address 1]
  //   Read Data 2 = Register File[Read Address 2]
  //   If load:
  //   	Register File[Write Address] = Write Data
  //   Tip:
  //   Start with the design for RAM8.
  //   Then, extend it to work with separate read addresses and write addresses 
endmodule

module RAM64 (
  input  [15:0] in,
  input  [5:0] address,
  input  load,
  output [15:0] out
);

  wire demultiplexer_1_out0, demultiplexer_1_out1, demultiplexer_1_out2, demultiplexer_1_out3,
       demultiplexer_1_out4, demultiplexer_1_out5, demultiplexer_1_out6, demultiplexer_1_out7;
  wire [15:0] ram8_1_out, ram8_2_out, ram8_3_out, ram8_4_out, ram8_5_out, ram8_6_out, ram8_7_out, ram8_8_out;

  // Probe on address[5:3]
  // Probe on address[2:0]
  Demultiplexer #(.enable("false"), .select(3)) demultiplexer_1 (
    .out0(demultiplexer_1_out0), .out1(demultiplexer_1_out1), .out2(demultiplexer_1_out2),
    .out3(demultiplexer_1_out3), .out4(demultiplexer_1_out4), .out5(demultiplexer_1_out5),
    .out6(demultiplexer_1_out6), .out7(demultiplexer_1_out7), .in(load), .sel(address[5:3]));
  RAM8 ram8_1 (.load(demultiplexer_1_out0), .address(address[2:0]), .in(in), .out(ram8_1_out));
  RAM8 ram8_2 (.load(demultiplexer_1_out1), .address(address[2:0]), .in(in), .out(ram8_2_out));
  RAM8 ram8_3 (.load(demultiplexer_1_out2), .address(address[2:0]), .in(in), .out(ram8_3_out));
  RAM8 ram8_4 (.load(demultiplexer_1_out3), .address(address[2:0]), .in(in), .out(ram8_4_out));
  RAM8 ram8_5 (.load(demultiplexer_1_out4), .address(address[2:0]), .in(in), .out(ram8_5_out));
  RAM8 ram8_6 (.load(demultiplexer_1_out5), .address(address[2:0]), .in(in), .out(ram8_6_out));
  RAM8 ram8_7 (.load(demultiplexer_1_out6), .address(address[2:0]), .in(in), .out(ram8_7_out));
  RAM8 ram8_8 (.load(demultiplexer_1_out7), .address(address[2:0]), .in(in), .out(ram8_8_out));
  Multiplexer #(.enable("false"), .select(3), .width(16)) multiplexer_1 (
    .in0(ram8_1_out), .in1(ram8_2_out), .in2(ram8_3_out), .in3(ram8_4_out), .in4(ram8_5_out),
    .in5(ram8_6_out), .in6(ram8_7_out), .in7(ram8_8_out), .out(out), .sel(address[5:3]));

  // Notes on the sheet:
  //   A memory bank of arbitrary length (a power of 2) can be built recursively from smaller memory units, all the way
  //   down to the single register level. A 64-register RAM can be built from an array of eight 8-register RAM
  //   chips. To select a particular register from the RAM64 memory, you can use a 6-bit address, say xxxyyy. 
  //   The MSB xxx bits select one of the RAM8 chips, and the LSB yyy bits select one of the registers within the
  //   selected RAM8. The RAM64 chip should be equipped with logic circuits that enable this hierarchical
  //   addressing scheme.
  //   which RAM8
endmodule

module PC (
  input  [15:0] in,
  input  reset,
  input  load,
  input  inc,
  output [15:0] out
);

  wire clock_1_out;
  wire [15:0] adder_1_out, multiplexer_1_out, multiplexer_2_out, multiplexer_3_out;

  Multiplexer #(.enable("false"), .width(16)) multiplexer_1 (
    .in0(adder_1_out), .in1({16{1'b0}}), .out(multiplexer_1_out), .sel(reset));
  Multiplexer #(.enable("false"), .width(16)) multiplexer_2 (
    .in0(multiplexer_1_out), .in1(in), .out(multiplexer_2_out), .sel(load));
  Register #(.width(16)) register_1 (.D(multiplexer_2_out), .clk(clock_1_out), .Q(out));  // open: en, clr
  Clock clock_1 (.out(clock_1_out));
  Multiplexer #(.enable("false"), .width(16)) multiplexer_3 (
    .in0({16{1'b0}}), .in1(16'h1), .out(multiplexer_3_out), .sel(inc));
  Adder #(.width(16)) adder_1 (.a(out), .b(multiplexer_3_out), .out(adder_1_out));  // open: cin, cout

  // Notes on the sheet:
  //   Function:
  //   If reset(t-1) then out(t) = 0
  //   	else if load(t-1) then out(t) = in(t-1)
  //   		else if inc(t-1) then out(t) =(t-1) + 1
  //   			else out(t) = out(t-1)
  //   A w-bit counter consists of two main elements:
  //   a regular w-bit register, and combinational logic. The combinational logic is designed to  
  //   (a) compute the counting function, and 
  //   (b) put the counter in the right operating mode, as dictated by the values
  //   of its three control bits.
  //   Tip: Use multiplexers, and the Inc16 component located in Assignment 4 Components.
  //   You do not need to use the Write Enable port on the Built-In Register for this task.
  //   First, attempt to create the Program Counter that has a single control bit "inc", then incorporate
  //   the load and finally reset control bits.
  //   NOTE for grader: I couldnt get the import of inc16 to 
  //   work so i just have the built in one
endmodule

module Inc16 (
  input  [15:0] in,
  output [15:0] out,
  output carry
);

  Adder #(.width(16)) adder_1 (.a(in), .b(16'h1), .out(out), .cout(carry));  // open: cin

  // Notes on the sheet:
  //   16-bit incrementer.
  //   out = in + 1
  //   Use a constant (Wiring>Constant) for this
endmodule
