// Logisim project Assignment4_b.circ as structural Verilog: 4 circuits, main circuit RAM512
module RAM64 (
  input  [5:0] address,
  input  load,
  input  [15:0] in,
  output [15:0] out
);

  wire clock_1_out;

  RAM #(.addrWidth(6), .dataWidth(16)) ram_1 (
    .addr(address), .we(load), .clk(clock_1_out), .din(in), .dout(out));  // open: oe
  Clock clock_1 (.out(clock_1_out));

  // Notes on the sheet:
  //   With the recursive approach for building RAM, there are too many gates for the simulator, and this leads to performance
  //   issues. For this reason, we have separated the assignment into two halves. This subcircuit is already completed and uses
  //   the built-in RAM module.
  //   RAM64 x 64 means that the address space has 64 registers, each containing 16 bits. Write-Enable is the same
  //   as the Load Input. C3 is for a clock input (you will need to connect a clock). The rightmost port is the output
  //   data, the upper left port is the address and the bottom left port is the incoming data.
  //   You will use the built-in RAM for a future assignment. I recommend playing around with it!
endmodule

module RAM512 (
  input  load,
  input  [8:0] address,
  input  [15:0] in,
  output [15:0] out
);

  wire demultiplexer_1_out0, demultiplexer_1_out1, demultiplexer_1_out2, demultiplexer_1_out3,
       demultiplexer_1_out4, demultiplexer_1_out5, demultiplexer_1_out6, demultiplexer_1_out7;
  wire [15:0] ram64_1_out, ram64_2_out, ram64_3_out, ram64_4_out, ram64_5_out, ram64_6_out, ram64_7_out,
       ram64_8_out;

  Demultiplexer #(.enable("false"), .select(3)) demultiplexer_1 (
    .out0(demultiplexer_1_out0), .out1(demultiplexer_1_out1), .out2(demultiplexer_1_out2),
    .out3(demultiplexer_1_out3), .out4(demultiplexer_1_out4), .out5(demultiplexer_1_out5),
    .out6(demultiplexer_1_out6), .out7(demultiplexer_1_out7), .in(load), .sel(address[8:6]));
  // Probe on address[8:6]
  // Probe on address[5:0]
  RAM64 ram64_1 (.address(address[5:0]), .load(demultiplexer_1_out0), .in(in), .out(ram64_1_out));
  RAM64 ram64_2 (.address(address[5:0]), .load(demultiplexer_1_out1), .in(in), .out(ram64_2_out));
  RAM64 ram64_3 (.address(address[5:0]), .load(demultiplexer_1_out2), .in(in), .out(ram64_3_out));
  RAM64 ram64_4 (.address(address[5:0]), .load(demultiplexer_1_out3), .in(in), .out(ram64_4_out));
  RAM64 ram64_5 (.address(address[5:0]), .load(demultiplexer_1_out4), .in(in), .out(ram64_5_out));
  RAM64 ram64_6 (.address(address[5:0]), .load(demultiplexer_1_out5), .in(in), .out(ram64_6_out));
  RAM64 ram64_7 (.address(address[5:0]), .load(demultiplexer_1_out6), .in(in), .out(ram64_7_out));
  RAM64 ram64_8 (.address(address[5:0]), .load(demultiplexer_1_out7), .in(in), .out(ram64_8_out));
  Multiplexer #(.enable("false"), .select(3), .width(16)) multiplexer_1 (
    .in0(ram64_1_out), .in1(ram64_2_out), .in2(ram64_3_out), .in3(ram64_4_out), .in4(ram64_5_out),
    .in5(ram64_6_out), .in6(ram64_7_out), .in7(ram64_8_out), .out(out), .sel(address[8:6]));

  // Notes on the sheet:
  //   which ram64 (most 
  //   significant 3 bits of addy)
  //   RAM512 can be built out of multiple RAM64 chips in a similar fashion to how
  //   RAM64 was constructed.
endmodule

module RAM4K (
  input  load,
  input  [11:0] address,
  input  [15:0] in,
  output [15:0] out
);

  wire demultiplexer_1_out0, demultiplexer_1_out1, demultiplexer_1_out2, demultiplexer_1_out3,
       demultiplexer_1_out4, demultiplexer_1_out5, demultiplexer_1_out6, demultiplexer_1_out7;
  wire [15:0] ram512_1_out, ram512_2_out, ram512_3_out, ram512_4_out, ram512_5_out, ram512_6_out,
       ram512_7_out, ram512_8_out;

  // Probe on address[8:0]
  // Probe on address[11:9]
  Demultiplexer #(.enable("false"), .select(3)) demultiplexer_1 (
    .out0(demultiplexer_1_out0), .out1(demultiplexer_1_out1), .out2(demultiplexer_1_out2),
    .out3(demultiplexer_1_out3), .out4(demultiplexer_1_out4), .out5(demultiplexer_1_out5),
    .out6(demultiplexer_1_out6), .out7(demultiplexer_1_out7), .in(load), .sel(address[11:9]));
  RAM512 ram512_1 (.load(demultiplexer_1_out0), .address(address[8:0]), .in(in), .out(ram512_1_out));
  RAM512 ram512_2 (.load(demultiplexer_1_out1), .address(address[8:0]), .in(in), .out(ram512_2_out));
  RAM512 ram512_3 (.load(demultiplexer_1_out2), .address(address[8:0]), .in(in), .out(ram512_3_out));
  RAM512 ram512_4 (.load(demultiplexer_1_out3), .address(address[8:0]), .in(in), .out(ram512_4_out));
  RAM512 ram512_5 (.load(demultiplexer_1_out4), .address(address[8:0]), .in(in), .out(ram512_5_out));
  RAM512 ram512_6 (.load(demultiplexer_1_out5), .address(address[8:0]), .in(in), .out(ram512_6_out));
  RAM512 ram512_7 (.load(demultiplexer_1_out6), .address(address[8:0]), .in(in), .out(ram512_7_out));
  RAM512 ram512_8 (.load(demultiplexer_1_out7), .address(address[8:0]), .in(in), .out(ram512_8_out));
  Multiplexer #(.enable("false"), .select(3), .width(16)) multiplexer_1 (
    .in0(ram512_1_out), .in1(ram512_2_out), .in2(ram512_3_out), .in3(ram512_4_out), .in4(ram512_5_out),
    .in5(ram512_6_out), .in6(ram512_7_out), .in7(ram512_8_out), .out(out), .sel(address[11:9]));

  // Notes on the sheet:
  //   Use the previously implemented RAM512 chip for this chip
  //   address of ram512 chip
  //   which ram512 (3 most 
  //   significant digits of addy)
endmodule

module RAM16K (
  input  load,
  input  [14:0] address,
  input  [15:0] in,
  output [15:0] out
);

  wire demultiplexer_1_out0, demultiplexer_1_out1, demultiplexer_1_out2, demultiplexer_1_out3,
       demultiplexer_1_out4, demultiplexer_1_out5, demultiplexer_1_out6, demultiplexer_1_out7;
  wire [15:0] ram4k_1_out, ram4k_2_out, ram4k_3_out, ram4k_4_p4, ram4k_5_out, ram4k_6_out, ram4k_7_out,
       ram4k_8_out;

  // Probe on address[11:0]
  // Probe on address[14:12]
  Demultiplexer #(.enable("false"), .select(3)) demultiplexer_1 (
    .out0(demultiplexer_1_out0), .out1(demultiplexer_1_out1), .out2(demultiplexer_1_out2),
    .out3(demultiplexer_1_out3), .out4(demultiplexer_1_out4), .out5(demultiplexer_1_out5),
    .out6(demultiplexer_1_out6), .out7(demultiplexer_1_out7), .in(load), .sel(address[14:12]));
  RAM4K ram4k_1 (.load(demultiplexer_1_out0), .address(address[11:0]), .in(in), .out(ram4k_1_out));
  RAM4K ram4k_2 (.load(demultiplexer_1_out1), .address(address[11:0]), .in(in), .out(ram4k_2_out));
  RAM4K ram4k_3 (.load(demultiplexer_1_out2), .address(address[11:0]), .in(in), .out(ram4k_3_out));
  // RAM4K ram4k_4: pin names not known; wires that end beside it: demultiplexer_1_out3, address[11:0], in, ram4k_4_p4
  RAM4K ram4k_5 (.load(demultiplexer_1_out4), .address(address[11:0]), .in(in), .out(ram4k_5_out));
  RAM4K ram4k_6 (.load(demultiplexer_1_out5), .address(address[11:0]), .in(in), .out(ram4k_6_out));
  RAM4K ram4k_7 (.load(demultiplexer_1_out6), .address(address[11:0]), .in(in), .out(ram4k_7_out));
  RAM4K ram4k_8 (.load(demultiplexer_1_out7), .address(address[11:0]), .in(in), .out(ram4k_8_out));
  Multiplexer #(.enable("false"), .select(3), .width(16)) multiplexer_1 (
    .in0(ram4k_1_out), .in1(ram4k_2_out), .in2(ram4k_3_out), .in3(ram4k_4_p4), .in4(ram4k_5_out),
    .in5(ram4k_6_out), .in6(ram4k_7_out), .in7(ram4k_8_out), .out(out), .sel(address[14:12]));

  // Notes on the sheet:
  //   Use the previously implemented RAM4K for this chip.
  //   address of ram4k chip
  //   which ram4k (3 most 
  //   significant digits of addy)
endmodule
